// Logisim project mycircekw.circ as structural Verilog: 1 circuit, main circuit main
module main (
  input  Midi_or_Buzzer,
  input  [6:0] Volume,
  output [7:0] out_3,
  output [7:0] out_4,
  output [15:0] out_5,
  output [7:0] out_6,
  output [7:0] out_7
);

  wire BE, controlled_buffer_2_out, mckeyboard_1_p5, mckeyboard_2_p1, mckeyboard_3_p1, mckeyboard_3_p2,
       not_1_out, sound_emitter_1_p1, sound_emitter_1_p2, sound_emitter_1_p3, sound_emitter_1_p4,
       sound_emitter_2_p1, sound_emitter_2_p2, sound_emitter_2_p3, sound_emitter_2_p4, sound_emitter_3_p1,
       sound_emitter_3_p2, sound_emitter_3_p3, sound_emitter_4_p1, sound_emitter_4_p2, sound_emitter_4_p3,
       sound_emitter_4_p4, sound_emitter_4_p13;
  wire [7:0] controlled_buffer_1_out, mckeyboard_1_p1, mckeyboard_1_p2, mckeyboard_1_p3, mckeyboard_1_p4,
       mckeyboard_2_p5, mckeyboard_2_p6, mckeyboard_2_p7, mckeyboard_2_p8, mckeyboard_3_p4, mckeyboard_3_p5,
       mckeyboard_3_p6, mckeyboard_3_p7;

  assign out_4 = mckeyboard_2_p7 | mckeyboard_3_p6 | mckeyboard_1_p3;  // OR_Gate or_1, 8 bits wide
  assign out_6 = mckeyboard_2_p6 | mckeyboard_3_p5 | mckeyboard_1_p2;  // OR_Gate or_2, 8 bits wide
  assign out_7 = mckeyboard_2_p5 | mckeyboard_3_p4 | mckeyboard_1_p1;  // OR_Gate or_3, 8 bits wide
  // MCKeyboard mckeyboard_1: pin names not known; wires that end beside it: mckeyboard_1_p1, mckeyboard_1_p2, mckeyboard_1_p3, mckeyboard_1_p4, mckeyboard_1_p5
  // MCKeyboard mckeyboard_2: pin names not known; wires that end beside it: mckeyboard_2_p1, BE, out_5, mckeyboard_2_p1, mckeyboard_2_p5, mckeyboard_2_p6, mckeyboard_2_p7, mckeyboard_2_p8
  // MCKeyboard mckeyboard_3: pin names not known; wires that end beside it: mckeyboard_3_p1, mckeyboard_3_p2, mckeyboard_3_p1, mckeyboard_3_p4, mckeyboard_3_p5, mckeyboard_3_p6, mckeyboard_3_p7, mckeyboard_3_p2
  // sound_emitter sound_emitter_1: pin names not known; wires that end beside it: sound_emitter_1_p1, sound_emitter_1_p2, sound_emitter_1_p3, sound_emitter_1_p4, sound_emitter_1_p1, sound_emitter_1_p2, out_4, sound_emitter_1_p3, sound_emitter_1_p4
  // sound_emitter sound_emitter_2: pin names not known; wires that end beside it: sound_emitter_2_p1, sound_emitter_2_p2, sound_emitter_2_p3, sound_emitter_2_p4, sound_emitter_2_p1, sound_emitter_2_p2, out_6, sound_emitter_2_p3, sound_emitter_2_p4
  // sound_emitter sound_emitter_3: pin names not known; wires that end beside it: sound_emitter_3_p1, sound_emitter_3_p2, sound_emitter_3_p3, sound_emitter_3_p1, sound_emitter_3_p2, out_7, sound_emitter_3_p3, mckeyboard_1_p5
  assign controlled_buffer_1_out = not_1_out ? mckeyboard_1_p4 : 8'bz;  // Controlled_Buffer controlled_buffer_1
  not not_1 (not_1_out, Midi_or_Buzzer);
  assign out_3 = mckeyboard_3_p7 | mckeyboard_2_p8 | controlled_buffer_1_out;  // OR_Gate or_4, 8 bits wide
  assign controlled_buffer_2_out = Midi_or_Buzzer ? BE : 1'bz;  // Controlled_Buffer controlled_buffer_2
  // sound_emitter sound_emitter_4: pin names not known; wires that end beside it: sound_emitter_4_p1, sound_emitter_4_p2, sound_emitter_4_p3, sound_emitter_4_p4, sound_emitter_4_p1, sound_emitter_4_p2, out_3, sound_emitter_4_p3, sound_emitter_4_p4, out_5, controlled_buffer_2_out, Volume, sound_emitter_4_p13
  Clock clock_1 (.out(sound_emitter_4_p13));

  // Other names for the same wires on the sheet: BF[15:0] = out_5

  // Notes on the sheet:
  //   Percussion
  //   Tubular Bell
  //   Vibraphone
  //   Church Organ
  //   Close Encounters of the Third Kind is:
  //   D6 E6 C6 C5 G5
  //   D8 E8 C8 C7 G7
  //   or:
  //   etc.
endmodule
